# Fritzing sketch RGB_LED_test (saved by Fritzing 0.9.3b)
breadboards: 1

parts:
  Part1 = Arduino Uno (Rev3)
  LED1 = RGB LED (com. anode, rbg) [package="5 mm [THT]"]

nets:
  N1: Part1.D9_PWM, LED1.red_cathode
  N2: Part1.D10_PWM/SS, LED1.blue_cathode
  N3: Part1.D11_PWM/MOSI, LED1.green_cathode
  N4: Part1.5V, LED1.common_anode
