# Fritzing sketch potBlink (saved by Fritzing 0.9.3b)
breadboards: 1

parts:
  R1 = Rotary Potentiometer (Small) [maximum_resistance=100kΩ package=THT]
  Part1 = Arduino Uno (Rev3)
  LED1 = LED - 5mm [color="Red (633nm)" package="5 mm [THT]"]
  R2 = Resistor [tolerance=±5% resistance=220 package=THT]
  S1 = Toggle Switch [package=THT]

nets:
  N1: R1.leg1, Part1.GND, LED1.cathode, S1.L2
  N2: R1.wiper, Part1.A0
  N3: R1.leg2, Part1.D12/MISO
  N4: Part1.D11_PWM/MOSI, S1.COM
  N5: Part1.D13/SCK, R2.Pin_1
  N6: Part1.5V, S1.L1
  N7: LED1.anode, R2.Pin_0
