# Fritzing sketch pseudoTheremin (saved by Fritzing 0.9.3b)
breadboards: 1

parts:
  R1 = Photocell (LDR) [package=THT]
  J1 = Piezo Speaker
  Part1 = Arduino Uno (Rev3)
  R2 = Resistor [tolerance=±5% resistance=220 package=THT]

nets:
  N1: R1.pin_0, Part1.A0, R2.Pin_1
  N2: R1.pin_1, Part1.5V
  N3: J1.pin1, Part1.GND, R2.Pin_0
  N4: J1.pin2, Part1.D12/MISO
