# Fritzing sketch trinketMCP9808Reader (saved by Fritzing 0.9.3b)
breadboards: 1

parts:
  Part1 = MCP9808 High Accuracy I2C Temperature Sensor [part_number=1782]
  Part2 = Adafruit Trinket M0 [part_number="Adafruit #3500"]

nets:
  N1: Part1.VDD, Part2.VBUS
  GND: Part1.GND, Part2.GND
  N2: Part1.SCL, Part2.D2_A1_PA09_SCL_MISO
  N3: Part1.SDA, Part2.D0_A4_PA08_SDA

custom parts:
  MCP9808 High Accuracy I2C Temperature Sensor: This I2C digital temperature sensor is one of the more accurate/precise we've ever seen, with a typical accuracy of ±0.25°C over the sensor's -40°C to +125°C range and precision of +0.0625°C. They work great with any microcontroller using standard i2c. There are 3 address pins so you can connect up to 8 to a single I2C bus without address collisions. Best of all, a wide voltage range makes is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
