# Fritzing sketch photocellRead (saved by Fritzing 0.9.3b)
breadboards: 1

parts:
  Part1 = Adafruit Trinket M0 [part_number="Adafruit #3500"]
  R1 = Photocell (LDR) [package=THT]
  R2 = Resistor [tolerance=±5% resistance=220 package=THT]

nets:
  N1: Part1.GND, R2.Pin_0
  N2: Part1.3.3V, R1.pin_1
  N3: Part1.D2_A1_PA09_SCL_MISO, R1.pin_0, R2.Pin_1
