# Fritzing sketch 5vVoltageRegCircuit (saved by Fritzing 0.9.3b)
circuit board: 8.46667cm x 5.64444cm
breadboards: 1

parts:
  IC1 = Voltage Regulator [package=to220-igo]
  D1 = Rectifier Diode [part_number=1N4001 package="300 mil [THT]"]
  D2 = Rectifier Diode [part_number=1N4001 package="300 mil [THT]"]
  C1 = Electrolytic Capacitor [capacitance=47µF voltage=35V package="100 mil [THT, electrolytic]"]
  C2 = Electrolytic Capacitor [capacitance=47µF voltage=35V package="100 mil [THT, electrolytic]"]

nets:
  N1: IC1.GND, C1.-, C2.-
  N2: IC1.IN, D1.cathode, C1.+
  N3: IC1.OUT, D2.anode, C2.+
